// Logisim project cancer-lgn-binary.circ as structural Verilog: 1 circuit, main circuit main
module main (
  input  _1,
  input  _2,
  input  _3,
  input  _4,
  input  _5,
  input  _6,
  input  _7,
  input  _8,
  output out_9,
  output out_10,
  output out_11,
  output out_12,
  output out_13,
  output out_14,
  output out_15,
  output out_16
);

  wire L1G1_out, L1G2_out, L1G3_out, L1G4_out, L1G5_out, L1G6_out, L1G7_out, L1G8_out, L2G1_out, L2G2_out,
       L2G3_out, L2G4_out, L2G5_out, L2G6_out, L2G7_out, L3G1_out, L3G2_out, L3G4_out, L3G5_out, L3G6_out,
       L3G7_out, not_1_out, not_2_out, not_3_out, not_4_out, not_5_out, not_6_out, not_7_out, not_8_out,
       not_9_out;

  not not_1 (not_1_out, _5);
  and L1G1 (L1G1_out, _1, _2);
  nor L1G2 (L1G2_out, _2, _5);
  not not_2 (not_2_out, _4);
  not L1G3 (L1G3_out, not_2_out);
  or L1G4 (L1G4_out, _2, _6);
  and L1G5 (L1G5_out, not_1_out, _2);
  not not_3 (not_3_out, _7);
  not L1G6 (L1G6_out, not_3_out);
  xor L1G7 (L1G7_out, _1, _8);
  not L1G8 (L1G8_out, _4);
  not not_4 (not_4_out, L1G6_out);
  nor L2G1 (L2G1_out, L1G1_out, L1G5_out);
  and L2G2 (L2G2_out, L1G4_out, not_4_out);
  not L2G3 (L2G3_out, L1G2_out);
  not L2G4 (L2G4_out, L1G8_out);
  and L2G7 (L2G7_out, L1G3_out, L1G6_out);
  // OR_Gate L2G8 has open pins: in0=L1G7_out, in1=L1G3_out, out=open
  not not_5 (not_5_out, L2G3_out);
  xnor L2G5 (L2G5_out, L1G5_out, L1G7_out);
  xnor L2G6 (L2G6_out, L1G7_out, L1G1_out);
  or L3G1 (L3G1_out, L2G2_out, L2G5_out);
  not not_6 (not_6_out, L2G4_out);
  and L3G5 (L3G5_out, not_5_out, L2G2_out);
  not L3G6 (L3G6_out, L2G6_out);
  or L3G7 (L3G7_out, L2G7_out, L2G5_out);
  not not_7 (not_7_out, L2G1_out);
  nor L3G2 (L3G2_out, L2G4_out, L2G7_out);
  // NOR_Gate L3G3 is placed but not wired
  not L3G4 (L3G4_out, not_6_out);
  // NOT_Gate L3G8 has open pins: in=not_7_out, out=open
  not not_8 (not_8_out, L3G2_out);
  not not_9 (not_9_out, L3G5_out);
  and L4G1 (out_9, L3G5_out, not_7_out);
  and L4G2 (out_10, not_8_out, L3G4_out);
  not L4G3 (out_11, L3G2_out);
  not L4G4 (out_12, not_9_out);
  nor L4G5 (out_13, L3G6_out, L3G5_out);
  not L4G6 (out_14, L3G4_out);
  and L4G7 (out_15, 1'b0, 1'b0, L3G1_out);
  or L4G8 (out_16, L3G4_out, L3G7_out);
endmodule
