// Logisim project numericalclusterfinal.circ as structural Verilog: 1 circuit, main circuit main
module main (
  input  bit_1,
  input  bit_2,
  input  bit_3,
  input  bit_4,
  input  bit_5,
  input  bit_6,
  input  bit_7,
  input  bit_8,
  output out_9,
  output out_10,
  output out_11,
  output out_12,
  output out_13,
  output out_14,
  output out_15,
  output out_16
);

  wire L1G1_out, L1G3_out, L1G4_out, L1G5_out, L1G6_out, L1G7_out, L1G8_out, L2G1_out, L2G2_out, L2G4_out,
       L2G5_out, L2G6_out, L2G7_out, L3G1_out, L3G2_out, L3G4_out, L3G5_out, L3G6_out, L3G8_out, not_1_out,
       not_2_out, not_3_out, not_4_out, not_5_out, not_6_out, not_7_out, not_8_out;

  xnor L1G1 (L1G1_out, bit_1, bit_2);
  // XOR_Gate L1G2 has open pins: in3=bit_2, in4=bit_5, out=open
  or L1G3 (L1G3_out, bit_2, bit_4);
  or L1G4 (L1G4_out, bit_2, bit_6);
  or L1G5 (L1G5_out, bit_2, bit_5);
  nand L1G6 (L1G6_out, bit_7, bit_1);
  or L1G7 (L1G7_out, bit_1, bit_8);
  nand L1G8 (L1G8_out, bit_1, bit_4);
  not not_1 (not_1_out, L1G6_out);
  not not_2 (not_2_out, L1G7_out);
  and L2G1 (L2G1_out, L1G1_out, L1G5_out);
  or L2G2 (L2G2_out, L1G4_out, not_1_out);
  not L2G4 (L2G4_out, L1G8_out);
  or L2G5 (L2G5_out, L1G7_out, L1G5_out);
  or L2G6 (L2G6_out, L1G1_out, not_2_out);
  and L2G7 (L2G7_out, not_1_out, L1G3_out);
  // OR_Gate L2G8 has open pins: in1=L1G3_out, in3=L1G7_out, out=open
  not not_3 (not_3_out, L2G2_out);
  not not_4 (not_4_out, L2G4_out);
  not not_5 (not_5_out, L2G1_out);
  not L3G1 (L3G1_out, not_3_out);
  nor L3G2 (L3G2_out, L2G4_out, L2G7_out);
  // NOR_Gate L3G3 has open pins: in1=L2G1_out, in3=L2G6_out, out=open
  not L3G4 (L3G4_out, not_4_out);
  not L3G5 (L3G5_out, L2G2_out);
  not L3G6 (L3G6_out, L2G6_out);
  // OR_Gate L3G7 has open pins: in2=L2G5_out, in3=L2G7_out, out=open
  not L3G8 (L3G8_out, not_5_out);
  and L4G1 (out_9, L3G5_out, not_6_out);
  not not_6 (not_6_out, L3G8_out);
  not not_7 (not_7_out, L3G2_out);
  and L4G2 (out_10, not_7_out, L3G4_out);
  not L4G3 (out_11, L3G2_out);
  not not_8 (not_8_out, L3G5_out);
  not L4G4 (out_12, not_8_out);
  nor L4G5 (out_13, L3G5_out, L3G6_out);
  not L4G6 (out_14, L3G4_out);
  and L4G7 (out_15, L3G1_out, L3G2_out);
  not L4G8 (out_16, L3G4_out);
endmodule
